// Logisim project ex2.circ as structural Verilog: 1 circuit, main circuit compute_BrUn
module compute_BrUn (
  input  [31:0] INSTRUCTION,
  output BrUn
);

  wire comparator_1_eq;
  wire [18:0] bit_extender_1_out;

  Comparator #(.width(7)) comparator_1 (.a(7'b1100011), .b(INSTRUCTION[6:0]), .eq(comparator_1_eq));  // open: gt, lt
  assign bit_extender_1_out = {{18{INSTRUCTION[31]}}, INSTRUCTION[31]};  // Bit_Extender bit_extender_1
  and and_1 (BrUn, comparator_1_eq, INSTRUCTION[13]);
endmodule
